# Fritzing sketch Blink Led Bicolor (saved by Fritzing 0.9.3b)
breadboards: 1

parts:
  LED1 = DUO LED RG [package="5 mm [THT]"]
  Componente1 = Arduino Uno (Rev3)
  R1 = Resistor [tolerance=±5% resistance=220 package=THT]

nets:
  N1: LED1.red_anode, Componente1.D8
  N2: LED1.common_cathode, R1.Pin_0
  N3: LED1.green_anode, Componente1.D13/SCK
  N4: Componente1.GND, R1.Pin_1
